// Logisim project 4bit_ALU.circ as structural Verilog: 1 circuit, main circuit alu
module alu (
  input  [3:0] A,
  input  [3:0] B,
  input  [1:0] ALUOp,
  output [3:0] C
);

  wire [3:0] H, tunnel, tunnel_t, Y;

  Adder #(.width(4)) adder_1 (.a(A), .b(B), .out(tunnel));  // open: cin, cout
  Subtractor #(.width(4)) subtractor_1 (.a(A), .b(B), .out(tunnel_t));  // open: bin, bout
  assign Y = A & B;  // AND_Gate and_1, 4 bits wide
  assign H = A | B;  // OR_Gate or_1, 4 bits wide
  Multiplexer #(.select(2), .width(4)) multiplexer_1 (
    .in0(tunnel), .in1(tunnel_t), .in2(Y), .in3(H), .out(C), .sel(ALUOp));  // open: en

  // Other names for the same wires on the sheet: OP[1:0] = ALUOp

  // Notes on the sheet:
  //   输入
  //   加减与或
  //   ALU
endmodule
