// Logisim project CRC.circ as structural Verilog: 2 circuits, main circuit 4bit_mod2
module _4bit_mod2 (
  input  [3:0] a,
  input  [3:0] b,
  output [2:0] c,
  output d
);

  wire [2:0] _1YS;
  wire [3:3] xor_1_out;

  assign {xor_1_out[3], _1YS} = a ^ b;  // XOR_Gate xor_1, 4 bits wide
  Multiplexer #(.width(3)) multiplexer_1 (.in0(a[2:0]), .in1(_1YS), .out(c), .sel(a[3]));  // open: en

  assign d = a[3];

  // Other names for the same wires on the sheet: _2YS[2:0] = a[2:0]; BCS[3:0] = a; S = a[3]; cs[3:0] = b; YS[2:0] = c

  // Notes on the sheet:
  //   输入
  //   被除数位数管理
  //   最高位为1时余数
  //   被除数最高位对应的余数
  //   输出
endmodule

module CRC (
  input  [7:0] A,
  input  [3:0] B,
  output [10:0] C
);

  wire [2:0] n4bit_mod2_1_c, n4bit_mod2_2_c, n4bit_mod2_3_c, n4bit_mod2_4_c, n4bit_mod2_5_c, n4bit_mod2_6_c,
       n4bit_mod2_7_c;

  _4bit_mod2 u_4bit_mod2_1 (.a(A[7:4]), .b(B), .c(n4bit_mod2_1_c));  // open: d
  _4bit_mod2 u_4bit_mod2_2 (.a({n4bit_mod2_1_c, A[3]}), .b(B), .c(n4bit_mod2_2_c));  // open: d
  _4bit_mod2 u_4bit_mod2_3 (.a({n4bit_mod2_2_c, A[2]}), .b(B), .c(n4bit_mod2_3_c));  // open: d
  _4bit_mod2 u_4bit_mod2_4 (.a({n4bit_mod2_3_c, A[1]}), .b(B), .c(n4bit_mod2_4_c));  // open: d
  _4bit_mod2 u_4bit_mod2_5 (.a({n4bit_mod2_4_c, A[0]}), .b(B), .c(n4bit_mod2_5_c));  // open: d
  _4bit_mod2 u_4bit_mod2_6 (.a({n4bit_mod2_5_c, 1'b0}), .b(B), .c(n4bit_mod2_6_c));  // open: d
  _4bit_mod2 u_4bit_mod2_7 (.a({n4bit_mod2_6_c, 1'b0}), .b(B), .c(n4bit_mod2_7_c));  // open: d
  _4bit_mod2 u_4bit_mod2_8 (.a({n4bit_mod2_7_c, 1'b0}), .b(B), .c(C[2:0]));  // open: d

  assign C[10:3] = A;

  // Other names for the same wires on the sheet: _8_3[10:0] = {A, C[2:0]}; YSJZ[10:3] = A; CS[3:0] = B

  // Notes on the sheet:
  //   输入
  //   输出
endmodule
