// Logisim project FSM.circ as structural Verilog: 1 circuit, main circuit fsm
module fsm (
  input  CLR,
  input  [1:0] In,
  output Z
);

  wire and_1_out, and_2_out, and_3_out, and_4_out, CLK, not_1_out, not_2_out, not_3_out, not_4_out,
       not_5_out, not_6_out, not_7_out, not_8_out, not_9_out, s0, s1, s10, s11;
  wire [1:0] multiplexer_1_out;

  Clock u_CLK (.out(CLK));
  Multiplexer #(.width(2)) multiplexer_1 (
    .in0({s11, s10}), .in1(2'b00), .out(multiplexer_1_out), .sel(CLR));  // open: en
  not not_1 (not_1_out, s1);
  not not_2 (not_2_out, In[0]);
  not not_3 (not_3_out, s0);
  not not_4 (not_4_out, In[0]);
  not not_5 (not_5_out, In[1]);
  not not_6 (not_6_out, s0);
  not not_7 (not_7_out, In[0]);
  not not_8 (not_8_out, s0);
  not not_9 (not_9_out, In[0]);
  Register #(.width(2)) register_1 (.D(multiplexer_1_out), .Q({s1, s0}), .clk(CLK));  // open: en, clr
  and and_1 (and_1_out, not_1_out, s0, not_2_out);
  or or_1 (s11, and_1_out, and_2_out);
  and and_2 (and_2_out, s1, not_3_out, not_4_out);
  and and_3 (and_3_out, not_5_out, In[0]);
  or or_2 (s10, and_3_out, and_4_out);
  and and_4 (and_4_out, s1, not_6_out, not_7_out);
  and and_5 (Z, s1, not_8_out, not_9_out);

  // Other names for the same wires on the sheet: SR[1:0] = {s11, s10}

  // Notes on the sheet:
  //   输入
  //   状态转换
  //   输出
endmodule
