// Logisim project GRF.circ as structural Verilog: 1 circuit, main circuit grf
module grf (
  input  clk,
  input  reset,
  input  WE,
  input  [4:0] A1,
  input  [4:0] A2,
  input  [4:0] A3,
  input  [31:0] WD,
  output [31:0] RD1,
  output [31:0] RD2
);

  wire _0, _0c, _1, _1c, _2, _2c, _3, _3c, _4, _4c, _5, _5c, _6, _6c, _7, _7c, _8, _8c, _9, _9c, _10, _10c,
       _11, _11c, _12, _12c, _13, _13c, _14, _14c, _15, _15c, _16, _16c, _17, _17c, _18, _18c, _19, _19c,
       _20, _20c, _21, _21c, _22, _22c, _23, _23c, _24, _24c, _25, _25c, _26, _26c, _27, _27c, _28, _28c,
       _29, _29c, _30, _30c, _31, _31c;
  wire [31:0] _0q, _1q, _2q, _3q, _4q, _5q, _6q, _7q, _8q, _9q, _10q, _11q, _12q, _13q, _14q, _15q, _16q,
       _17q, _18q, _19q, _20q, _21q, _22q, _23q, _24q, _25q, _26q, _27q, _28q, _29q, _30q, _31q;

  Decoder #(.select(5)) decoder_1 (
    .out0(_0), .out1(_1), .out2(_2), .out3(_3), .out4(_4), .out5(_5), .out6(_6), .out7(_7), .out8(_8),
    .out9(_9), .out10(_10), .out11(_11), .out12(_12), .out13(_13), .out14(_14), .out15(_15), .out16(_16),
    .out17(_17), .out18(_18), .out19(_19), .out20(_20), .out21(_21), .out22(_22), .out23(_23), .out24(_24),
    .out25(_25), .out26(_26), .out27(_27), .out28(_28), .out29(_29), .out30(_30), .out31(_31), .sel(A3));  // open: en
  and u__0 (_0c, WE, _0);
  and u__1 (_1c, WE, _1);
  and u__2 (_2c, WE, _2);
  and u__3 (_3c, WE, _3);
  and u__4 (_4c, WE, _4);
  and u__5 (_5c, WE, _5);
  and u__6 (_6c, WE, _6);
  and u__7 (_7c, WE, _7);
  and u__8 (_8c, WE, _8);
  and u__9 (_9c, WE, _9);
  and u__10 (_10c, WE, _10);
  and u__11 (_11c, WE, _11);
  and u__12 (_12c, WE, _12);
  and u__13 (_13c, WE, _13);
  and u__14 (_14c, WE, _14);
  and u__15 (_15c, WE, _15);
  and u__16 (_16c, WE, _16);
  and u__17 (_17c, WE, _17);
  and u__18 (_18c, WE, _18);
  and u__19 (_19c, WE, _19);
  and u__20 (_20c, WE, _20);
  and u__21 (_21c, WE, _21);
  and u__22 (_22c, WE, _22);
  and u__23 (_23c, WE, _23);
  and u__24 (_24c, WE, _24);
  and u__25 (_25c, WE, _25);
  and u__26 (_26c, WE, _26);
  and u__27 (_27c, WE, _27);
  and u__28 (_28c, WE, _28);
  and u__29 (_29c, WE, _29);
  and u__30 (_30c, WE, _30);
  and u__31 (_31c, WE, _31);
  Register #(.width(32)) _0_2 (.D({32{1'b0}}), .en(_0c), .Q(_0q));  // open: clk, clr
  Register #(.width(32)) _1_2 (.D(WD), .en(_1c), .Q(_1q), .clk(clk), .clr(reset));
  Register #(.width(32)) _2_2 (.D(WD), .en(_2c), .Q(_2q), .clk(clk), .clr(reset));
  Register #(.width(32)) _3_2 (.D(WD), .en(_3c), .Q(_3q), .clk(clk), .clr(reset));
  Register #(.width(32)) _4_2 (.D(WD), .en(_4c), .Q(_4q), .clk(clk), .clr(reset));
  Register #(.width(32)) _5_2 (.D(WD), .en(_5c), .Q(_5q), .clk(clk), .clr(reset));
  Register #(.width(32)) _6_2 (.D(WD), .en(_6c), .Q(_6q), .clk(clk), .clr(reset));
  Register #(.width(32)) _7_2 (.D(WD), .en(_7c), .Q(_7q), .clk(clk), .clr(reset));
  Register #(.width(32)) _8_2 (.D(WD), .en(_8c), .Q(_8q), .clk(clk), .clr(reset));
  Register #(.width(32)) _9_2 (.D(WD), .en(_9c), .Q(_9q), .clk(clk), .clr(reset));
  Register #(.width(32)) _10_2 (.D(WD), .en(_10c), .Q(_10q), .clk(clk), .clr(reset));
  Register #(.width(32)) _11_2 (.D(WD), .en(_11c), .Q(_11q), .clk(clk), .clr(reset));
  Register #(.width(32)) _12_2 (.D(WD), .en(_12c), .Q(_12q), .clk(clk), .clr(reset));
  Register #(.width(32)) _13_2 (.D(WD), .en(_13c), .Q(_13q), .clk(clk), .clr(reset));
  Register #(.width(32)) _14_2 (.D(WD), .en(_14c), .Q(_14q), .clk(clk), .clr(reset));
  Register #(.width(32)) _15_2 (.D(WD), .en(_15c), .Q(_15q), .clk(clk), .clr(reset));
  Register #(.width(32)) _16_2 (.D(WD), .en(_16c), .Q(_16q), .clk(clk), .clr(reset));
  Register #(.width(32)) _17_2 (.D(WD), .en(_17c), .Q(_17q), .clk(clk), .clr(reset));
  Register #(.width(32)) _18_2 (.D(WD), .en(_18c), .Q(_18q), .clk(clk), .clr(reset));
  Register #(.width(32)) _19_2 (.D(WD), .en(_19c), .Q(_19q), .clk(clk), .clr(reset));
  Register #(.width(32)) _20_2 (.D(WD), .en(_20c), .Q(_20q), .clk(clk), .clr(reset));
  Register #(.width(32)) _21_2 (.D(WD), .en(_21c), .Q(_21q), .clk(clk), .clr(reset));
  Register #(.width(32)) _22_2 (.D(WD), .en(_22c), .Q(_22q), .clk(clk), .clr(reset));
  Register #(.width(32)) _23_2 (.D(WD), .en(_23c), .Q(_23q), .clk(clk), .clr(reset));
  Register #(.width(32)) _24_2 (.D(WD), .en(_24c), .Q(_24q), .clk(clk), .clr(reset));
  Register #(.width(32)) _25_2 (.D(WD), .en(_25c), .Q(_25q), .clk(clk), .clr(reset));
  Register #(.width(32)) _26_2 (.D(WD), .en(_26c), .Q(_26q), .clk(clk), .clr(reset));
  Register #(.width(32)) _27_2 (.D(WD), .en(_27c), .Q(_27q), .clk(clk), .clr(reset));
  Register #(.width(32)) _28_2 (.D(WD), .en(_28c), .Q(_28q), .clk(clk), .clr(reset));
  Register #(.width(32)) _29_2 (.D(WD), .en(_29c), .Q(_29q), .clk(clk), .clr(reset));
  Register #(.width(32)) _30_2 (.D(WD), .en(_30c), .Q(_30q), .clk(clk), .clr(reset));
  Register #(.width(32)) _31_2 (.D(WD), .en(_31c), .Q(_31q), .clk(clk), .clr(reset));
  Multiplexer #(.select(5), .width(32)) multiplexer_1 (
    .in0(_0q), .in1(_1q), .in2(_2q), .in3(_3q), .in4(_4q), .in5(_5q), .in6(_6q), .in7(_7q), .in8(_8q),
    .in9(_9q), .in10(_10q), .in11(_11q), .in12(_12q), .in13(_13q), .in14(_14q), .in15(_15q), .in16(_16q),
    .in17(_17q), .in18(_18q), .in19(_19q), .in20(_20q), .in21(_21q), .in22(_22q), .in23(_23q), .in24(_24q),
    .in25(_25q), .in26(_26q), .in27(_27q), .in28(_28q), .in29(_29q), .in30(_30q), .in31(_31q), .out(RD1),
    .sel(A1));  // open: en
  Multiplexer #(.select(5), .width(32)) multiplexer_2 (
    .in0(_0q), .in1(_1q), .in2(_2q), .in3(_3q), .in4(_4q), .in5(_5q), .in6(_6q), .in7(_7q), .in8(_8q),
    .in9(_9q), .in10(_10q), .in11(_11q), .in12(_12q), .in13(_13q), .in14(_14q), .in15(_15q), .in16(_16q),
    .in17(_17q), .in18(_18q), .in19(_19q), .in20(_20q), .in21(_21q), .in22(_22q), .in23(_23q), .in24(_24q),
    .in25(_25q), .in26(_26q), .in27(_27q), .in28(_28q), .in29(_29q), .in30(_30q), .in31(_31q), .out(RD2),
    .sel(A2));  // open: en

  // Notes on the sheet:
  //   输入
  //   输出
endmodule
