// Logisim project 4人抢答.circ as structural Verilog: 1 circuit, main circuit main
module main (
  input  reset,
  input  in_2,
  input  in_3,
  input  in_4,
  input  in_5
);

  wire and_1_out, and_2_out, and_3_out, and_4_out, and_5_out, and_6_out, and_7_out, and_8_out, clock_1_out,
       d_ff_1_q, d_ff_1_qn, d_ff_2_q, d_ff_2_qn, d_ff_3_q, d_ff_3_qn, d_ff_4_q, d_ff_4_qn, not_1_out,
       not_2_out, not_3_out, not_4_out;

  and and_1 (and_1_out, in_2, d_ff_2_qn, d_ff_3_qn, d_ff_4_qn);
  and and_2 (and_2_out, in_3, d_ff_1_qn, d_ff_3_qn, d_ff_4_qn);
  and and_3 (and_3_out, in_4, d_ff_1_qn, d_ff_2_qn, d_ff_4_qn);
  and and_4 (and_4_out, in_5, d_ff_1_qn, d_ff_2_qn, d_ff_3_qn);
  D_Flip_Flop d_ff_1 (.clk(not_1_out), .D(and_1_out), .Q(d_ff_1_q), .Qn(d_ff_1_qn), .reset(reset));  // open: preset, en
  LED led_1 (.in(d_ff_1_q));
  LED led_2 (.in(d_ff_2_q));
  D_Flip_Flop d_ff_2 (.clk(not_2_out), .D(and_2_out), .Q(d_ff_2_q), .Qn(d_ff_2_qn), .reset(reset));  // open: preset, en
  LED led_3 (.in(d_ff_3_q));
  D_Flip_Flop d_ff_3 (.clk(not_3_out), .D(and_3_out), .Q(d_ff_3_q), .Qn(d_ff_3_qn), .reset(reset));  // open: preset, en
  LED led_4 (.in(d_ff_4_q));
  D_Flip_Flop d_ff_4 (.clk(not_4_out), .D(and_4_out), .Q(d_ff_4_q), .Qn(d_ff_4_qn), .reset(reset));  // open: preset, en
  Clock clock_1 (.out(clock_1_out));
  and and_5 (and_5_out, d_ff_1_qn, clock_1_out);
  and and_6 (and_6_out, d_ff_2_qn, clock_1_out);
  and and_7 (and_7_out, d_ff_3_qn, clock_1_out);
  and and_8 (and_8_out, d_ff_4_qn, clock_1_out);
  not not_1 (not_1_out, and_5_out);
  not not_2 (not_2_out, and_6_out);
  not not_3 (not_3_out, and_7_out);
  not not_4 (not_4_out, and_8_out);
endmodule
