// Logisim project fbnq.circ as structural Verilog: 3 circuits, main circuit main
module main (
  input  [2:0] N,
  output [3:0] Nth
);

  wire clock_1_out, comparator_1_eq, comparator_1_gt, or_1_out;
  wire [3:0] bit_extender_1_out, counter_1_q, cz_1_out_3, jf_1_out_3, jf_1_out_4, multiplexer_2_out,
       register_1_q, register_2_q;

  assign bit_extender_1_out = {{1{1'b0}}, N};  // Bit_Extender bit_extender_1
  Clock clock_1 (.out(clock_1_out));
  Counter #(.width(4), .max('hf), .ongoal("stay")) counter_1 (
    .Q(counter_1_q), .clk(clock_1_out));  // open: load, D, count, carry, clr
  Register #(.width(4)) register_1 (.D(multiplexer_2_out), .Q(register_1_q), .clk(clock_1_out));  // open: en, clr
  Register #(.width(4)) register_2 (.D(jf_1_out_4), .Q(register_2_q), .clk(clock_1_out));  // open: en, clr
  cz cz_1 (.in_1(register_2_q), .in_2(counter_1_q), .out_3(cz_1_out_3));
  Comparator #(.width(4), .mode("unsigned")) comparator_1 (
    .a(counter_1_q), .b(bit_extender_1_out), .gt(comparator_1_gt), .eq(comparator_1_eq));  // open: lt
  Multiplexer #(.width(4)) multiplexer_1 (.in0(4'b0000), .in1(register_1_q), .out(Nth), .sel(or_1_out));  // open: en
  or or_1 (or_1_out, comparator_1_gt, comparator_1_eq);
  JF jf_1 (.in_1(register_1_q), .in_2(cz_1_out_3), .out_3(jf_1_out_3), .out_4(jf_1_out_4));
  Multiplexer #(.width(4)) multiplexer_2 (
    .in0(jf_1_out_3), .in1(register_1_q), .out(multiplexer_2_out), .sel(or_1_out));  // open: en
endmodule

module JF (
  input  [3:0] in_1,
  input  [3:0] in_2,
  output [3:0] out_3,
  output [3:0] out_4
);

  Adder #(.width(4)) adder_1 (.a(in_1), .b(in_2), .out(out_4));  // open: cin, cout

  assign out_3 = in_2;
endmodule

module cz (
  input  [3:0] in_1,
  input  [3:0] in_2,
  output [3:0] out_3
);

  Multiplexer #(.select(4), .width(4)) multiplexer_1 (
    .in0(4'b0001), .in1(in_1), .in2(in_1), .in3(in_1), .in4(in_1), .in5(in_1), .in6(in_1), .in7(in_1),
    .out(out_3), .sel(in_2));  // open: in8, in9, in10, in11, in12, in13, in14, in15, en
endmodule
