// Logisim project mod5.circ as structural Verilog: 2 circuits, main circuit mod5
module mod5 (
  input  In,
  output S0,
  output S1,
  output S2,
  output S3,
  output S4
);

  wire clock_1_out, register_1_q, register_2_q, register_3_q;
  wire [2:0] fsm_1_l5;

  Clock clock_1 (.out(clock_1_out));
  Register #(.width(1)) register_1 (.D(fsm_1_l5[2]), .Q(register_1_q), .clk(clock_1_out));  // open: en, clr
  Register #(.width(1)) register_2 (.D(fsm_1_l5[1]), .Q(register_2_q), .clk(clock_1_out));  // open: en, clr
  Register #(.width(1)) register_3 (.D(fsm_1_l5[0]), .Q(register_3_q), .clk(clock_1_out));  // open: en, clr
  FSM fsm_1 (
    .L0(register_1_q), .L1(register_2_q), .L2(register_3_q), .B(In), .L3(fsm_1_l5[2]), .L4(fsm_1_l5[1]),
    .L5(fsm_1_l5[0]));
  Decoder #(.select(3)) decoder_1 (
    .out0(S0), .out1(S1), .out2(S2), .out3(S3), .out4(S4), .sel(fsm_1_l5));  // open: out5, out6, out7, en
endmodule

module FSM (
  input  L0,
  input  L1,
  input  L2,
  input  B,
  output L3,
  output L4,
  output L5
);

  wire and_1_out, and_2_out, and_3_out, and_4_out, and_5_out, and_6_out, not_1_out, not_2_out, not_3_out,
       not_4_out, not_5_out, not_6_out, not_7_out, not_8_out, not_9_out;

  not not_1 (not_1_out, L0);
  not not_2 (not_2_out, B);
  not not_3 (not_3_out, B);
  not not_4 (not_4_out, L0);
  not not_5 (not_5_out, L1);
  not not_6 (not_6_out, B);
  not not_7 (not_7_out, L0);
  not not_8 (not_8_out, L2);
  not not_9 (not_9_out, B);
  and and_1 (and_1_out, not_1_out, L1, not_2_out);
  and and_2 (and_2_out, L0, L2, not_3_out);
  and and_3 (and_3_out, not_4_out, not_5_out, not_6_out);
  and and_4 (and_4_out, not_7_out, L1, B);
  and and_5 (and_5_out, L0, not_8_out, not_9_out);
  and and_6 (and_6_out, L0, L2, B);
  or or_1 (L3, and_1_out, and_2_out);
  or or_2 (L5, and_3_out, and_4_out, and_5_out, and_6_out);

  assign L4 = B;
endmodule
