// Logisim project P3最终版.circ as structural Verilog: 6 circuits, main circuit GRF
module main (
  input  reset,
  output [31:0] out_2,
  output out_3,
  output [4:0] out_4,
  output [31:0] out_5,
  output out_6,
  output [4:0] out_7,
  output [31:0] out_8
);

  wire _1, alu_1_blez, alu_1_zero, ALUSrc, bptal, bptalyes, Branch, clk, J, jal, jr, lbu_t, MemtoReg,
       multiplexer_6_out, or_1_out, or_2_out, PCSrc, RegDst;
  wire [1:0] addr_1__0, BOp, EXTOp;
  wire [2:0] ALUOp;
  wire [4:0] multiplexer_1_out;
  wire [29:5] alu_1_aluresult;
  wire [31:0] bit_extender_1_out, bit_extender_2_out, bit_extender_3_out, bit_extender_4_out, ext_1_b,
       grf_1_rd1, LBU, multiplexer_4_out, multiplexer_5_out, multiplexer_7_out, PC_1, ram_1_data,
       shifter_1_out;

  Clock u_clk (.out(clk));
  IFU ifu_1 (
    .Instr(out_2), .imm(out_2[15:0]), .PCSrc(PCSrc), .addeess(out_2[25:0]), .J(J), .reset(reset), .clk(clk),
    .PC_1(PC_1), .jr(jr), .rs(out_2[25:21]));
  and and_1 (_1, bptal, bptalyes);
  or or_1 (or_1_out, _1, jal);
  Multiplexer #(.width(5)) multiplexer_1 (
    .in0(out_2[20:16]), .in1(out_2[15:11]), .out(multiplexer_1_out), .sel(RegDst));  // open: en
  // Probe on out_2[15:0]
  // Probe on EXTOp
  Multiplexer #(.width(5)) multiplexer_2 (
    .in0(multiplexer_1_out), .in1({5{1'b1}}), .out(out_4), .sel(or_1_out));  // open: en
  EXT ext_1 (.A(out_2[15:0]), .B(ext_1_b), .EXTOp(EXTOp));
  Shifter #(.width(32)) shifter_1 (.in(PC_1), .\dist (5'b00010), .out(shifter_1_out));
  Multiplexer #(.width(32)) multiplexer_3 (
    .in0(multiplexer_5_out), .in1(shifter_1_out), .out(out_5), .sel(or_1_out));  // open: en
  or or_2 (or_2_out, _1, out_3);
  GRF grf_1 (
    .A1(out_2[25:21]), .A2(out_2[20:16]), .A3(out_4), .WD(out_5), .RD1(grf_1_rd1), .RD2(out_8), .clk(clk),
    .reset(reset), .WE(or_2_out));
  // Probe on ext_1_b
  // Probe on multiplexer_4_out
  Multiplexer #(.width(32)) multiplexer_4 (
    .in0(out_8), .in1(ext_1_b), .out(multiplexer_4_out), .sel(ALUSrc));  // open: en
  Multiplexer #(.width(32)) multiplexer_5 (
    .in0(multiplexer_7_out), .in1(LBU), .out(multiplexer_5_out), .sel(lbu_t));  // open: en
  Controller controller_1 (
    .func(out_2[5:0]), .Op(out_2[31:26]), .EXTOp(EXTOp), .MemtoReg(MemtoReg), .ALUOp(ALUOp), .Branch(Branch),
    .ALUSrc(ALUSrc), .RegDst(RegDst), .RegWrite(out_3), .MemWrite(out_6), .J(J), .jal(jal), .lbu(lbu_t),
    .BOp(BOp), .bptal(bptal), .jr(jr));
  // Probe on grf_1_rd1
  ALU alu_1 (
    .A(grf_1_rd1), .B(multiplexer_4_out), .zero(alu_1_zero), .ALUresult({alu_1_aluresult, out_7, addr_1__0}),
    .ALUOp(ALUOp), .blez(alu_1_blez), .bptal(bptalyes));
  Multiplexer #(.select(2)) multiplexer_6 (
    .in0(alu_1_zero), .in1(alu_1_blez), .in2(bptalyes), .out(multiplexer_6_out), .sel(BOp));  // open: in3, en
  RAM #(.addrWidth(5), .dataWidth(32), .bus("separate")) ram_1 (
    .addr(out_7), .din(out_8), .data(ram_1_data), .str(out_6), .clk(clk), .clr(reset));  // open: sel, ld
  and and_2 (PCSrc, Branch, multiplexer_6_out);
  Multiplexer #(.width(32)) multiplexer_7 (
    .in0({alu_1_aluresult, out_7, addr_1__0}), .in1(ram_1_data), .out(multiplexer_7_out), .sel(MemtoReg));  // open: en
  assign bit_extender_1_out = {{24{1'b0}}, ram_1_data[7:0]};  // Bit_Extender bit_extender_1
  assign bit_extender_2_out = {{24{1'b0}}, ram_1_data[15:8]};  // Bit_Extender bit_extender_2
  assign bit_extender_3_out = {{24{1'b0}}, ram_1_data[23:16]};  // Bit_Extender bit_extender_3
  assign bit_extender_4_out = {{24{1'b0}}, ram_1_data[31:24]};  // Bit_Extender bit_extender_4
  // Probe on LBU
  Multiplexer #(.select(2), .width(32)) multiplexer_8 (
    .in0(bit_extender_1_out), .in1(bit_extender_2_out), .in2(bit_extender_3_out), .in3(bit_extender_4_out),
    .out(LBU), .sel(addr_1__0));  // open: en
  // Probe on out_2
  // Probe on out_4
  // Probe on out_5
  // Probe on out_7
  // Probe on out_8

  // Other names for the same wires on the sheet: MemAddr[4:0] = out_7; addeess[25:0] = out_2[25:0];
  //   func[5:0] = out_2[5:0]; imm[15:0] = out_2[15:0]; Instr[31:0] = out_2; rd[4:0] = out_2[15:11];
  //   rt[4:0] = out_2[20:16]; rs[4:0] = out_2[25:21]; Op[5:0] = out_2[31:26]; MemData[31:0] = out_8; MemWrite = out_6;
  //   RegAddr[4:0] = out_4; RegData[31:0] = out_5; RegWrite = out_3
endmodule

module GRF (
  input  clk,
  input  reset,
  input  WE,
  input  [4:0] A1,
  input  [4:0] A2,
  input  [4:0] A3,
  input  [31:0] WD,
  output [31:0] RD1,
  output [31:0] RD2
);

  wire _0, _0c, _1, _1c, _2, _2c, _3, _3c, _4, _4c, _5, _5c, _6, _6c, _7, _7c, _8, _8c, _9, _9c, _10, _10c,
       _11, _11c, _12, _12c, _13, _13c, _14, _14c, _15, _15c, _16, _16c, _17, _17c, _18, _18c, _19, _19c,
       _20, _20c, _21, _21c, _22, _22c, _23, _23c, _24, _24c, _25, _25c, _26, _26c, _27, _27c, _28, _28c,
       _29, _29c, _30, _30c, _31, _31c;
  wire [31:0] _0q, _1q, _2q, _3q, _4q, _5q, _6q, _7q, _8q, _9q, _10q, _11q, _12q, _13q, _14q, _15q, _16q,
       _17q, _18q, _19q, _20q, _21q, _22q, _23q, _24q, _25q, _26q, _27q, _28q, _29q, _30q, _31q;

  Decoder #(.select(5)) decoder_1 (
    .out0(_0), .out1(_1), .out2(_2), .out3(_3), .out4(_4), .out5(_5), .out6(_6), .out7(_7), .out8(_8),
    .out9(_9), .out10(_10), .out11(_11), .out12(_12), .out13(_13), .out14(_14), .out15(_15), .out16(_16),
    .out17(_17), .out18(_18), .out19(_19), .out20(_20), .out21(_21), .out22(_22), .out23(_23), .out24(_24),
    .out25(_25), .out26(_26), .out27(_27), .out28(_28), .out29(_29), .out30(_30), .out31(_31), .sel(A3));  // open: en
  and u__0 (_0c, WE, _0);
  and u__1 (_1c, WE, _1);
  and u__2 (_2c, WE, _2);
  and u__3 (_3c, WE, _3);
  and u__4 (_4c, WE, _4);
  and u__5 (_5c, WE, _5);
  and u__6 (_6c, WE, _6);
  and u__7 (_7c, WE, _7);
  and u__8 (_8c, WE, _8);
  and u__9 (_9c, WE, _9);
  and u__10 (_10c, WE, _10);
  and u__11 (_11c, WE, _11);
  and u__12 (_12c, WE, _12);
  and u__13 (_13c, WE, _13);
  and u__14 (_14c, WE, _14);
  and u__15 (_15c, WE, _15);
  and u__16 (_16c, WE, _16);
  and u__17 (_17c, WE, _17);
  and u__18 (_18c, WE, _18);
  and u__19 (_19c, WE, _19);
  and u__20 (_20c, WE, _20);
  and u__21 (_21c, WE, _21);
  and u__22 (_22c, WE, _22);
  and u__23 (_23c, WE, _23);
  and u__24 (_24c, WE, _24);
  and u__25 (_25c, WE, _25);
  and u__26 (_26c, WE, _26);
  and u__27 (_27c, WE, _27);
  and u__28 (_28c, WE, _28);
  and u__29 (_29c, WE, _29);
  and u__30 (_30c, WE, _30);
  and u__31 (_31c, WE, _31);
  Register #(.width(32)) _0_2 (.D({32{1'b0}}), .en(_0c), .Q(_0q));  // open: clk, clr
  Register #(.width(32)) _1_2 (.D(WD), .en(_1c), .Q(_1q), .clk(clk), .clr(reset));
  Register #(.width(32)) _2_2 (.D(WD), .en(_2c), .Q(_2q), .clk(clk), .clr(reset));
  Register #(.width(32)) _3_2 (.D(WD), .en(_3c), .Q(_3q), .clk(clk), .clr(reset));
  Register #(.width(32)) _4_2 (.D(WD), .en(_4c), .Q(_4q), .clk(clk), .clr(reset));
  Register #(.width(32)) _5_2 (.D(WD), .en(_5c), .Q(_5q), .clk(clk), .clr(reset));
  Register #(.width(32)) _6_2 (.D(WD), .en(_6c), .Q(_6q), .clk(clk), .clr(reset));
  Register #(.width(32)) _7_2 (.D(WD), .en(_7c), .Q(_7q), .clk(clk), .clr(reset));
  Register #(.width(32)) _8_2 (.D(WD), .en(_8c), .Q(_8q), .clk(clk), .clr(reset));
  Register #(.width(32)) _9_2 (.D(WD), .en(_9c), .Q(_9q), .clk(clk), .clr(reset));
  Register #(.width(32)) _10_2 (.D(WD), .en(_10c), .Q(_10q), .clk(clk), .clr(reset));
  Register #(.width(32)) _11_2 (.D(WD), .en(_11c), .Q(_11q), .clk(clk), .clr(reset));
  Register #(.width(32)) _12_2 (.D(WD), .en(_12c), .Q(_12q), .clk(clk), .clr(reset));
  Register #(.width(32)) _13_2 (.D(WD), .en(_13c), .Q(_13q), .clk(clk), .clr(reset));
  Register #(.width(32)) _14_2 (.D(WD), .en(_14c), .Q(_14q), .clk(clk), .clr(reset));
  Register #(.width(32)) _15_2 (.D(WD), .en(_15c), .Q(_15q), .clk(clk), .clr(reset));
  Register #(.width(32)) _16_2 (.D(WD), .en(_16c), .Q(_16q), .clk(clk), .clr(reset));
  Register #(.width(32)) _17_2 (.D(WD), .en(_17c), .Q(_17q), .clk(clk), .clr(reset));
  Register #(.width(32)) _18_2 (.D(WD), .en(_18c), .Q(_18q), .clk(clk), .clr(reset));
  Register #(.width(32)) _19_2 (.D(WD), .en(_19c), .Q(_19q), .clk(clk), .clr(reset));
  Register #(.width(32)) _20_2 (.D(WD), .en(_20c), .Q(_20q), .clk(clk), .clr(reset));
  Register #(.width(32)) _21_2 (.D(WD), .en(_21c), .Q(_21q), .clk(clk), .clr(reset));
  Register #(.width(32)) _22_2 (.D(WD), .en(_22c), .Q(_22q), .clk(clk), .clr(reset));
  Register #(.width(32)) _23_2 (.D(WD), .en(_23c), .Q(_23q), .clk(clk), .clr(reset));
  Register #(.width(32)) _24_2 (.D(WD), .en(_24c), .Q(_24q), .clk(clk), .clr(reset));
  Register #(.width(32)) _25_2 (.D(WD), .en(_25c), .Q(_25q), .clk(clk), .clr(reset));
  Register #(.width(32)) _26_2 (.D(WD), .en(_26c), .Q(_26q), .clk(clk), .clr(reset));
  Register #(.width(32)) _27_2 (.D(WD), .en(_27c), .Q(_27q), .clk(clk), .clr(reset));
  Register #(.width(32)) _28_2 (.D(WD), .en(_28c), .Q(_28q), .clk(clk), .clr(reset));
  Register #(.width(32)) _29_2 (.D(WD), .en(_29c), .Q(_29q), .clk(clk), .clr(reset));
  Register #(.width(32)) _30_2 (.D(WD), .en(_30c), .Q(_30q), .clk(clk), .clr(reset));
  Register #(.width(32)) _31_2 (.D(WD), .en(_31c), .Q(_31q), .clk(clk), .clr(reset));
  Multiplexer #(.select(5), .width(32)) multiplexer_1 (
    .in0(_0q), .in1(_1q), .in2(_2q), .in3(_3q), .in4(_4q), .in5(_5q), .in6(_6q), .in7(_7q), .in8(_8q),
    .in9(_9q), .in10(_10q), .in11(_11q), .in12(_12q), .in13(_13q), .in14(_14q), .in15(_15q), .in16(_16q),
    .in17(_17q), .in18(_18q), .in19(_19q), .in20(_20q), .in21(_21q), .in22(_22q), .in23(_23q), .in24(_24q),
    .in25(_25q), .in26(_26q), .in27(_27q), .in28(_28q), .in29(_29q), .in30(_30q), .in31(_31q), .out(RD1),
    .sel(A1));  // open: en
  Multiplexer #(.select(5), .width(32)) multiplexer_2 (
    .in0(_0q), .in1(_1q), .in2(_2q), .in3(_3q), .in4(_4q), .in5(_5q), .in6(_6q), .in7(_7q), .in8(_8q),
    .in9(_9q), .in10(_10q), .in11(_11q), .in12(_12q), .in13(_13q), .in14(_14q), .in15(_15q), .in16(_16q),
    .in17(_17q), .in18(_18q), .in19(_19q), .in20(_20q), .in21(_21q), .in22(_22q), .in23(_23q), .in24(_24q),
    .in25(_25q), .in26(_26q), .in27(_27q), .in28(_28q), .in29(_29q), .in30(_30q), .in31(_31q), .out(RD2),
    .sel(A2));  // open: en

  // Notes on the sheet:
  //   输入
  //   输出
endmodule

module ALU (
  input  [31:0] A,
  input  [2:0] ALUOp,
  input  [31:0] B,
  output blez,
  output zero,
  output [31:0] ALUresult,
  output bptal
);

  wire comparator_2_eq, comparator_2_lt;
  wire [31:0] adder_1_out, and_1_out, and_2_out, or_1_out, subtractor_1_out, subtractor_2_out;

  Adder #(.width(32)) adder_1 (.a(A), .b(B), .out(adder_1_out));  // open: cin, cout
  Subtractor #(.width(32)) subtractor_1 (.a(A), .b(B), .out(subtractor_1_out));  // open: bin, bout
  Subtractor #(.width(32)) subtractor_2 (.a(A), .b(32'h1), .out(subtractor_2_out));  // open: bin, bout
  assign and_1_out = A & B;  // AND_Gate and_1, 32 bits wide
  assign or_1_out = A | B;  // OR_Gate or_1, 32 bits wide
  assign and_2_out = subtractor_2_out & A;  // AND_Gate and_2, 32 bits wide
  Comparator #(.width(32)) comparator_1 (.a(and_2_out), .b({32{1'b0}}), .eq(bptal));  // open: gt, lt
  Multiplexer #(.select(3), .width(32)) multiplexer_1 (
    .in0(and_1_out), .in1(or_1_out), .in2(adder_1_out), .in3(subtractor_1_out), .in4(B),
    .in5({A[0], A[1], A[2], A[3], A[4], A[5], A[6], A[7], A[8], A[9], A[10], A[11], A[12], A[13], A[14], A[15], A[16], A[17], A[18], A[19], A[20], A[21], A[22], A[23], A[24], A[25], A[26], A[27], A[28], A[29], A[30], A[31]}),
    .out(ALUresult), .sel(ALUOp));  // open: in6, in7, en
  Comparator #(.width(32)) comparator_2 (
    .a(A), .b({32{1'b0}}), .eq(comparator_2_eq), .lt(comparator_2_lt));  // open: gt
  Comparator #(.width(32)) comparator_3 (.a(A), .b(B), .eq(zero));  // open: gt, lt
  or or_2 (blez, comparator_2_lt, comparator_2_eq);
endmodule

module IFU (
  input  [25:0] addeess,
  input  J,
  input  clk,
  input  reset,
  input  PCSrc,
  input  jr,
  input  [4:0] rs,
  input  [15:0] imm,
  output [31:0] Instr,
  output [31:0] PC_1
);

  wire [4:0] register_1_q;
  wire [26:0] register_1_q_2;
  wire [31:0] adder_1_out, bit_extender_2_out, multiplexer_1_out, multiplexer_2_out, multiplexer_3_out,
       or_1_out, rs_t, shifter_1_out;

  assign rs_t = {{27{1'b0}}, rs};  // Bit_Extender bit_extender_1
  assign bit_extender_2_out = {{16{imm[15]}}, imm};  // Bit_Extender bit_extender_2
  Multiplexer #(.width(32)) multiplexer_1 (
    .in0(PC_1), .in1(adder_1_out), .out(multiplexer_1_out), .sel(PCSrc));  // open: en
  Adder #(.width(32)) adder_1 (.a(PC_1), .b(bit_extender_2_out), .out(adder_1_out));  // open: cin, cout
  Multiplexer #(.width(32)) multiplexer_2 (
    .in0(multiplexer_1_out), .in1({2'b00, PC_1[31:28], addeess}), .out(multiplexer_2_out), .sel(J));  // open: en
  Multiplexer #(.width(32)) multiplexer_3 (
    .in0(multiplexer_2_out), .in1(rs_t), .out(multiplexer_3_out), .sel(jr));  // open: en
  Register #(.width(32)) register_1 (
    .D(multiplexer_3_out), .Q({register_1_q_2, register_1_q}), .clk(clk), .clr(reset));  // open: en
  Shifter #(.width(32), .shift("lr")) shifter_1 (.in(32'h3000), .\dist (5'b00010), .out(shifter_1_out));
  assign or_1_out = {register_1_q_2, register_1_q} | shifter_1_out;  // OR_Gate or_1, 32 bits wide
  Adder #(.width(32)) adder_2 (.a(or_1_out), .b(32'h1), .out(PC_1));  // open: cin, cout
  ROM #(.addrWidth(5), .dataWidth(32)) rom_1 (.addr(register_1_q), .data(Instr));  // open: sel

  // Other names for the same wires on the sheet: PC_1_31_28[3:0] = PC_1[31:28]
endmodule

module Controller (
  input  [5:0] func,
  input  [5:0] Op,
  output MemtoReg,
  output MemWrite,
  output Branch,
  output ALUSrc,
  output RegDst,
  output J,
  output jal,
  output lbu,
  output bptal,
  output jr,
  output [1:0] BOp,
  output [1:0] EXTOp,
  output RegWrite,
  output [2:0] ALUOp
);

  wire addu_out, beq_out, blez_out, bptal_out, j_out, jal_out, jr_out, LBU_out, lui_out, lw_out, not_1_out,
       not_2_out, not_3_out, not_4_out, not_5_out, not_6_out, not_7_out, not_8_out, not_9_out, not_10_out,
       not_11_out, not_12_out, ori_out, rev_out, subu_out, sw_out;

  not not_1 (not_1_out, func[4]);
  not not_2 (not_2_out, func[5]);
  not not_3 (not_3_out, func[2]);
  not not_4 (not_4_out, func[3]);
  not not_5 (not_5_out, func[0]);
  not not_6 (not_6_out, func[1]);
  not not_7 (not_7_out, Op[4]);
  not not_8 (not_8_out, Op[5]);
  not not_9 (not_9_out, Op[3]);
  not not_10 (not_10_out, Op[2]);
  not not_11 (not_11_out, Op[0]);
  not not_12 (not_12_out, Op[1]);
  and addu (addu_out, func[5], not_1_out, not_4_out, not_3_out, not_6_out, func[0], not_8_out, not_7_out, not_9_out, not_10_out, not_12_out, not_11_out);
  and subu (subu_out, func[5], not_1_out, not_4_out, not_3_out, func[1], func[0], not_8_out, not_7_out, not_9_out, not_10_out, not_12_out, not_11_out);
  and ori (ori_out, not_8_out, not_7_out, Op[3], Op[2], not_12_out, Op[0]);
  and lw (lw_out, Op[5], not_7_out, not_9_out, not_10_out, Op[1], Op[0]);
  and sw (sw_out, Op[5], not_7_out, Op[3], not_10_out, Op[1], Op[0]);
  and beq (beq_out, not_8_out, not_7_out, not_9_out, Op[2], not_12_out, not_11_out);
  and lui (lui_out, not_8_out, not_7_out, Op[3], Op[2], Op[1], Op[0]);
  and u_j (j_out, not_8_out, not_7_out, not_9_out, not_10_out, Op[1], not_11_out);
  and blez (blez_out, not_8_out, not_7_out, not_9_out, Op[2], Op[1], not_11_out);
  and u_jal (jal_out, not_8_out, not_7_out, not_9_out, not_10_out, Op[1], Op[0]);
  and u_LBU (LBU_out, Op[5], not_7_out, not_9_out, Op[2], not_12_out, not_11_out);
  and rev (rev_out, not_2_out, func[4], not_4_out, func[2], not_6_out, not_5_out, not_8_out, not_7_out, not_9_out, not_10_out, not_12_out, not_11_out);
  and u_bptal (bptal_out, not_8_out, not_7_out, not_9_out, not_10_out, not_12_out, Op[0]);
  and u_jr (jr_out, not_2_out, not_1_out, func[3], not_3_out, not_6_out, not_5_out, not_8_out, not_7_out, not_9_out, not_10_out, not_12_out, not_11_out);
  buf EXTOp1 (EXTOp[1], lui_out);  // OR_Gate
  or EXTOp0 (EXTOp[0], beq_out, lw_out, sw_out, blez_out, LBU_out, bptal_out);
  or u_MemtoReg (MemtoReg, lw_out, LBU_out);
  buf u_MemWrite (MemWrite, sw_out);  // OR_Gate
  or u_Branch (Branch, beq_out, blez_out, bptal_out);
  or ALUOp2 (ALUOp[2], lui_out, rev_out);
  or ALUOp1 (ALUOp[1], addu_out, subu_out, lw_out, sw_out, LBU_out);
  or ALUOp0 (ALUOp[0], subu_out, ori_out, rev_out);
  or u_ALUSrc (ALUSrc, ori_out, lw_out, sw_out, lui_out, LBU_out);
  or u_RegDst (RegDst, addu_out, subu_out, rev_out);
  or u_RegWrite (RegWrite, jal_out, addu_out, subu_out, ori_out, lw_out, lui_out, LBU_out, rev_out);
  or J_2 (J, j_out, jal_out);
  buf jal_2 (jal, jal_out);  // OR_Gate
  buf lbu_2 (lbu, LBU_out);  // OR_Gate
  buf BOp1 (BOp[1], bptal_out);  // OR_Gate
  buf BOp0 (BOp[0], blez_out);  // OR_Gate
  buf jr_2 (jr, jr_out);  // OR_Gate
  buf bptal_2 (bptal, bptal_out);  // OR_Gate
endmodule

module EXT (
  input  [15:0] A,
  input  [1:0] EXTOp,
  output [31:0] B
);

  wire [31:0] bit_extender_1_out, bit_extender_2_out;

  assign bit_extender_1_out = {{16{1'b0}}, A};  // Bit_Extender bit_extender_1
  assign bit_extender_2_out = {{16{A[15]}}, A};  // Bit_Extender bit_extender_2
  Multiplexer #(.select(2), .width(32)) multiplexer_1 (
    .in0(bit_extender_1_out), .in1(bit_extender_2_out), .in2({A, {16{1'b0}}}), .out(B), .sel(EXTOp));  // open: in3, en
endmodule
